// Logisim project criptoULA.circ as structural Verilog: 4 circuits, main circuit main
module main (
  input  [1:0] SEL,
  input  Criptografar___0___Decriptografar___1,
  input  [7:0] Chave_criptografica,
  output [6:0] out_4
);

  wire Clock, keyboard_1_avail, Reset_out;
  wire [6:0] bit_extender_2_out, keyboard_1_data;
  wire [7:0] charInput, charOutput;

  Keyboard keyboard_1 (.clk(Clock), .re(1'b1), .clr(Reset_out), .avail(keyboard_1_avail), .data(keyboard_1_data));
  Button Reset (.out(Reset_out));
  Clock clock_1 (.out(Clock));
  assign charInput = {{1{1'b0}}, keyboard_1_data};  // Bit_Extender bit_extender_1
  Bit_Extender #(.out_width(7)) bit_extender_2 (.in(charInput), .out(bit_extender_2_out));
  TTY tty_1 (.data(bit_extender_2_out), .clk(Clock), .we(keyboard_1_avail), .clr(Reset_out));
  ULA ula_1 (
    .A__caractere(charInput), .B__chave(Chave_criptografica), .\Operação (SEL), .Output(charOutput),
    .Modo(Criptografar___0___Decriptografar___1));
  Bit_Extender #(.out_width(7)) bit_extender_3 (.in(charOutput), .out(out_4));
  TTY tty_2 (.data(out_4), .clk(Clock), .we(keyboard_1_avail), .clr(Reset_out));

  // Other names for the same wires on the sheet: chave[7:0] = Chave_criptografica;
  //   modo = Criptografar___0___Decriptografar___1

  // Notes on the sheet:
  //   ENTRADA
  //   Digite o texto
  //   SELEÇÃO DE CRIPTOGRAFIA
  //   SELEÇAO DE MODO
  //   00 >> XOR
  //   01 >> CIFRA DE CÉSAR
  //   10 >> INVERSOR DE BITS
  //   11 >> PERMUTADOR DE BITS
  //   INPUT
  //   SAÍDA
  //   NÚCLEO CRIPTOGRÁFICO
  //   OUTPUT
endmodule

module ULA (
  input  [7:0] A__caractere,
  input  [7:0] B__chave,
  input  [1:0] \Operação ,
  input  Modo,
  output [7:0] Output
);

  wire [7:0] caesar_coder_1_output, caesar_decoder_1_p3, multiplexer_1_out, multiplexer_2_out, not_1_out,
       xor_1_out;

  assign xor_1_out = A__caractere ^ B__chave;  // XOR_Gate xor_1, 8 bits wide
  Caesar_coder caesar_coder_1 (
    .Caractere_ASCII_de_8_bits(A__caractere), .Deslocamento(B__chave), .Output(caesar_coder_1_output));
  // Caesar_decoder caesar_decoder_1: pin names not known; wires that end beside it: A__caractere, B__chave, caesar_decoder_1_p3
  assign not_1_out = ~A__caractere;  // NOT_Gate not_1, 8 bits wide
  Multiplexer #(.width(8), .enable("false")) multiplexer_1 (
    .in0(caesar_coder_1_output), .in1(caesar_decoder_1_p3), .out(multiplexer_1_out), .sel(Modo));
  Multiplexer #(.width(8), .enable("false")) multiplexer_2 (
    .in0({A__caractere[0], A__caractere[1], A__caractere[2], A__caractere[3], A__caractere[4], A__caractere[5], A__caractere[6], A__caractere[7]}),
    .in1({A__caractere[0], A__caractere[1], A__caractere[2], A__caractere[3], A__caractere[4], A__caractere[5], A__caractere[6], A__caractere[7]}),
    .out(multiplexer_2_out), .sel(Modo));
  Multiplexer #(.select(2), .width(8), .enable("false")) multiplexer_3 (
    .in0(xor_1_out), .in1(multiplexer_1_out), .in2(not_1_out), .in3(multiplexer_2_out), .out(Output),
    .sel(\Operação ));

  // Other names for the same wires on the sheet: A[7:0] = A__caractere; B[7:0] = B__chave; op[1:0] = \Operação 
endmodule

module Caesar_coder (
  input  [7:0] Caractere_ASCII_de_8_bits,
  input  [7:0] Deslocamento,
  output [7:0] Output
);

  Adder adder_1 (.a(Caractere_ASCII_de_8_bits), .b(Deslocamento), .out(Output));  // open: cin, cout
endmodule

module Caesar_decoder (
  input  [7:0] Caractere_ASCII_de_8_bits,
  input  [7:0] Deslocamento,
  output [7:0] Output
);

  Subtractor subtractor_1 (.a(Caractere_ASCII_de_8_bits), .b(Deslocamento), .out(Output));  // open: bin, bout
endmodule
